# Fritzing sketch MeArm_HC-06 (saved by Fritzing 0.9.2b)
breadboards: 1

parts:
  Part1 = Arduino Uno (Rev3)
  VCC1 = 4 x AAA Battery Mount  # not connected
  Part2 = Bluetooth HC-06 Macho
  R4 = Resistor [tolerance=±5% resistance=10k package=THT]
  R5 = Resistor [tolerance=±5% resistance=10k package=THT]
  R6 = Resistor [tolerance=±5% resistance=10k package=THT]

nets:
  N1: Part1.D0/RX, Part2.TXD
  5V: Part1.5V, Part2.VCC
  GND: Part1.GND, Part2.GND
  N2: Part2.RXD, R5.Pin_1, R6.Pin_0
  N3: R4.Pin_0, R6.Pin_1
